// Logisim project ALU.circ as structural Verilog: 17 circuits, main circuit shr16
module shr16 (
  input  [15:0] A,
  input  CIN,
  output COUT,
  output [15:0] OUTP
);


  assign COUT = A[0];
  assign OUTP = {CIN, A[15:1]};
endmodule

module shl16 (
  input  [15:0] A,
  input  CIN,
  output COUT,
  output [15:0] OUTP
);


  assign COUT = A[15];
  assign OUTP = {A[14:0], CIN};
endmodule

module rotl16 (
  input  [15:0] A,
  output [15:0] OUTP
);

  wire shl16_1_cout;

  shl16 shl16_1 (.A(A), .CIN(shl16_1_cout), .COUT(shl16_1_cout), .OUTP(OUTP));
endmodule

module rotr16 (
  input  [15:0] A,
  output [15:0] OUTP
);

  wire shr16_1_cout;

  shr16 shr16_1 (.A(A), .CIN(shr16_1_cout), .COUT(shr16_1_cout), .OUTP(OUTP));
endmodule

module add1 (
  input  A,
  input  B,
  input  CIN,
  output COUT,
  output OUTP
);

  wire and_1_out, and_2_out, xor_1_out;

  xor xor_1 (xor_1_out, A, B);
  and and_1 (and_1_out, B, A);
  and and_2 (and_2_out, xor_1_out, CIN);
  xor xor_2 (OUTP, xor_1_out, CIN);
  xor xor_3 (COUT, and_1_out, and_2_out);
endmodule

module add4 (
  input  [3:0] A,
  input  [3:0] B,
  input  CIN,
  output COUT,
  output [3:0] OUTP
);

  wire add1_1_cout, add1_2_cout, add1_3_cout;

  add1 add1_1 (.A(A[0]), .B(B[0]), .CIN(CIN), .COUT(add1_1_cout), .OUTP(OUTP[0]));
  add1 add1_2 (.A(A[1]), .B(B[1]), .CIN(add1_1_cout), .COUT(add1_2_cout), .OUTP(OUTP[1]));
  add1 add1_3 (.A(A[2]), .B(B[2]), .CIN(add1_2_cout), .COUT(add1_3_cout), .OUTP(OUTP[2]));
  add1 add1_4 (.A(A[3]), .B(B[3]), .CIN(add1_3_cout), .COUT(COUT), .OUTP(OUTP[3]));
endmodule

module add16 (
  input  [15:0] A,
  input  CIN,
  input  [15:0] B,
  output [15:0] OUTP,
  output COUT
);

  wire add4_1_cout, add4_2_cout, add4_3_cout;

  add4 add4_1 (.A(A[3:0]), .B(B[3:0]), .CIN(CIN), .COUT(add4_1_cout), .OUTP(OUTP[3:0]));
  add4 add4_2 (.A(A[7:4]), .B(B[7:4]), .CIN(add4_1_cout), .COUT(add4_2_cout), .OUTP(OUTP[7:4]));
  add4 add4_3 (.A(A[11:8]), .B(B[11:8]), .CIN(add4_2_cout), .COUT(add4_3_cout), .OUTP(OUTP[11:8]));
  add4 add4_4 (.A(A[15:12]), .B(B[15:12]), .CIN(add4_3_cout), .COUT(COUT), .OUTP(OUTP[15:12]));
endmodule

module decoder2 (
  input  ENA,
  input  [1:0] SEL,
  output [3:0] OUTP
);

  wire and_1_out, and_2_out, and_3_out, and_4_out, not_1_out, not_2_out;

  not not_1 (not_1_out, SEL[0]);
  not not_2 (not_2_out, SEL[1]);
  and and_1 (and_1_out, not_1_out, not_2_out);
  and and_2 (and_2_out, SEL[0], not_2_out);
  and and_3 (and_3_out, SEL[1], not_1_out);
  and and_4 (and_4_out, SEL[0], SEL[1]);
  and and_5 (OUTP[0], ENA, and_1_out);
  and and_6 (OUTP[1], ENA, and_2_out);
  and and_7 (OUTP[2], ENA, and_3_out);
  and and_8 (OUTP[3], ENA, and_4_out);
endmodule

module decoder4 (
  input  [3:0] SEL,
  input  ENA,
  output [15:0] OUTP
);

  wire [3:0] decoder2_1_outp;

  decoder2 decoder2_1 (.ENA(ENA), .SEL({SEL[2], SEL[3]}), .OUTP(decoder2_1_outp));
  decoder2 decoder2_2 (.ENA(decoder2_1_outp[0]), .SEL(SEL[1:0]), .OUTP(OUTP[3:0]));
  decoder2 decoder2_3 (.ENA(decoder2_1_outp[2]), .SEL(SEL[1:0]), .OUTP(OUTP[7:4]));
  decoder2 decoder2_4 (.ENA(decoder2_1_outp[1]), .SEL(SEL[1:0]), .OUTP(OUTP[11:8]));
  decoder2 decoder2_5 (.ENA(decoder2_1_outp[3]), .SEL(SEL[1:0]), .OUTP(OUTP[15:12]));

  // Other names for the same wires on the sheet: AB[1:0] = SEL[1:0]
endmodule

module comparator2 (
  input  [1:0] A,
  input  [1:0] B,
  output LT,
  output GT,
  output EQ
);

  wire nand_1_out, nand_2_out, nor_1_out, xnor_1_out, xor_1_out;

  xnor xnor_1 (xnor_1_out, B[1], A[1]);
  xor xor_1 (xor_1_out, B[0], A[0]);
  nor nor_1 (nor_1_out, B[1], xnor_1_out);
  nand nand_1 (nand_1_out, B[0], xor_1_out);
  nand nand_2 (nand_2_out, xnor_1_out, nand_1_out);
  xor xor_2 (LT, nor_1_out, nand_2_out);
  nor nor_2 (EQ, nand_2_out, xor_1_out);
  nor nor_3 (GT, LT, EQ);
endmodule

module comparator4 (
  input  [3:0] A,
  input  [3:0] B,
  output LT,
  output GT,
  output EQ
);

  wire and_1_out, comparator2_1_eq, comparator2_1_gt, comparator2_2_eq, comparator2_2_gt;

  comparator2 comparator2_1 (.A(A[3:2]), .B(B[3:2]), .GT(comparator2_1_gt), .EQ(comparator2_1_eq));  // open: LT
  comparator2 comparator2_2 (.A(A[1:0]), .B(B[1:0]), .GT(comparator2_2_gt), .EQ(comparator2_2_eq));  // open: LT
  and and_1 (and_1_out, comparator2_1_eq, comparator2_2_gt);
  and and_2 (EQ, comparator2_1_eq, comparator2_2_eq);
  or or_1 (GT, comparator2_1_gt, and_1_out);
  and and_3 (LT, ~GT, ~EQ);  // AND_Gate
endmodule

module comparator8 (
  input  [7:0] A,
  input  [7:0] B,
  output LT,
  output GT,
  output EQ
);

  wire and_1_out, comparator4_1_eq, comparator4_1_gt, comparator4_2_eq, comparator4_2_gt;

  comparator4 comparator4_1 (.A(A[7:4]), .B(B[7:4]), .GT(comparator4_1_gt), .EQ(comparator4_1_eq));  // open: LT
  comparator4 comparator4_2 (.A(A[3:0]), .B(B[3:0]), .GT(comparator4_2_gt), .EQ(comparator4_2_eq));  // open: LT
  and and_1 (and_1_out, comparator4_1_eq, comparator4_2_gt);
  and and_2 (EQ, comparator4_1_eq, comparator4_2_eq);
  or or_1 (GT, comparator4_1_gt, and_1_out);
  and and_3 (LT, ~GT, ~EQ);  // AND_Gate
endmodule

module comparator16 (
  input  [15:0] A,
  input  [15:0] B,
  output LT,
  output GT,
  output EQ
);

  wire and_1_out, comparator8_1_eq, comparator8_1_gt, comparator8_2_eq, comparator8_2_gt;

  comparator8 comparator8_1 (.A(A[15:8]), .B(B[15:8]), .GT(comparator8_1_gt), .EQ(comparator8_1_eq));  // open: LT
  comparator8 comparator8_2 (.A(A[7:0]), .B(B[7:0]), .GT(comparator8_2_gt), .EQ(comparator8_2_eq));  // open: LT
  and and_1 (and_1_out, comparator8_1_eq, comparator8_2_gt);
  and and_2 (EQ, comparator8_1_eq, comparator8_2_eq);
  or or_1 (GT, comparator8_1_gt, and_1_out);
  and and_3 (LT, ~GT, ~EQ);  // AND_Gate
endmodule

module ALU (
  input  [15:0] A,
  input  [15:0] B,
  input  CIN,
  input  [3:0] SEL,
  output OVER,
  output SIGN,
  output [15:0] HOUT,
  output [15:0] OUTP,
  output COUT,
  output LT,
  output GT,
  output EQ,
  output ZERO
);

  wire addsub16_1_cout, addsub16_1_over, ADDSUBINCDEC_COUT, D_ADD, D_AND, D_DEC, D_INC, D_NOT, D_OR, D_ROTL,
       D_ROTR, D_SHL, D_SHR, D_SUB, D_XOR, enable1_1_outp, not_1_out, or_1_out, or_2_out, or_5_out,
       shl16_1_cout, SHL_COUT, shr16_1_cout, SHR_COUT;
  wire [15:0] addsub16_1_outp, and_1_out, enable16_1_outp, enable16_2_outp, enable16_3_outp, enable16_4_outp,
       enable16_5_outp, enable16_6_outp, enable16_7_outp, enable16_8_outp, enable16_9_outp, enable16_10_outp,
       enable16_11_outp, not_2_out, or_3_out, or_4_out, rotl16_1_outp, rotr16_1_outp, shl16_1_outp,
       shr16_1_outp, xor_1_out;
  wire [15:12] decoder4_1_outp;

  enable1 enable1_1 (.I(CIN), .ENA(not_1_out), .OUTP(enable1_1_outp));
  enable16 enable16_1 (.ENA(or_2_out), .I(16'h1), .OUTP(enable16_1_outp));
  enable16 enable16_2 (.ENA(not_1_out), .I(B), .OUTP(enable16_2_outp));
  or or_1 (or_1_out, D_SUB, D_DEC);
  or or_2 (or_2_out, D_DEC, D_INC);
  assign or_3_out = enable16_1_outp | enable16_2_outp;  // OR_Gate or_3, 16 bits wide
  not not_1 (not_1_out, or_2_out);
  shr16 shr16_1 (.A(A), .CIN(CIN), .COUT(shr16_1_cout), .OUTP(shr16_1_outp));
  shl16 shl16_1 (.A(A), .CIN(CIN), .COUT(shl16_1_cout), .OUTP(shl16_1_outp));
  decoder4 decoder4_1 (
    .SEL(SEL), .ENA(1'b1),
    .OUTP({decoder4_1_outp, D_DEC, D_INC, D_SUB, D_ADD, D_ROTL, D_ROTR, D_SHL, D_SHR, D_NOT, D_AND, D_OR, D_XOR}));
  assign or_4_out = A | B;  // OR_Gate or_4, 16 bits wide
  assign and_1_out = A & B;  // AND_Gate and_1, 16 bits wide
  assign not_2_out = ~A;  // NOT_Gate not_2, 16 bits wide
  assign xor_1_out = A ^ B;  // XOR_Gate xor_1, 16 bits wide
  enable1 enable1_2 (.I(shr16_1_cout), .ENA(D_SHR), .OUTP(SHR_COUT));
  enable1 enable1_3 (.I(shl16_1_cout), .ENA(D_SHL), .OUTP(SHL_COUT));
  rotr16 rotr16_1 (.A(A), .OUTP(rotr16_1_outp));
  rotl16 rotl16_1 (.A(A), .OUTP(rotl16_1_outp));
  addsub16 addsub16_1 (
    .A(A), .B(or_3_out), .CIN(enable1_1_outp), .SUB(or_1_out), .OUTP(addsub16_1_outp),
    .COUT(addsub16_1_cout), .OVER(addsub16_1_over));
  enable1 enable1_4 (.I(addsub16_1_over), .ENA(or_5_out), .OUTP(OVER));
  enable16 enable16_3 (.ENA(D_XOR), .I(xor_1_out), .OUTP(enable16_3_outp));
  enable16 enable16_4 (.ENA(D_OR), .I(or_4_out), .OUTP(enable16_4_outp));
  enable16 enable16_5 (.ENA(D_AND), .I(and_1_out), .OUTP(enable16_5_outp));
  enable16 enable16_6 (.ENA(D_NOT), .I(not_2_out), .OUTP(enable16_6_outp));
  enable16 enable16_7 (.ENA(D_SHR), .I(shr16_1_outp), .OUTP(enable16_7_outp));
  enable16 enable16_8 (.ENA(D_SHL), .I(shl16_1_outp), .OUTP(enable16_8_outp));
  enable16 enable16_9 (.ENA(D_ROTR), .I(rotr16_1_outp), .OUTP(enable16_9_outp));
  enable16 enable16_10 (.ENA(D_ROTL), .I(rotl16_1_outp), .OUTP(enable16_10_outp));
  enable16 enable16_11 (.ENA(or_5_out), .I(addsub16_1_outp), .OUTP(enable16_11_outp));
  enable1 enable1_5 (.I(addsub16_1_cout), .ENA(or_5_out), .OUTP(ADDSUBINCDEC_COUT));
  or or_5 (or_5_out, D_ADD, D_SUB, D_INC, D_DEC);
  comparator16 comparator16_1 (.A(A), .B(B), .LT(LT), .GT(GT), .EQ(EQ));
  assign OUTP = enable16_3_outp | enable16_4_outp | enable16_5_outp | enable16_6_outp | enable16_7_outp | enable16_8_outp | enable16_9_outp | enable16_10_outp | enable16_11_outp;  // OR_Gate or_6, 16 bits wide
  or or_7 (COUT, SHR_COUT, SHL_COUT, ADDSUBINCDEC_COUT);
  comparator16 comparator16_2 (.A(OUTP), .B({16{1'b0}}), .EQ(ZERO));  // open: LT, GT

  assign HOUT = {16{1'b0}};
  assign SIGN = OUTP[15];

  // Other names for the same wires on the sheet: ADDSUBINCDEC_OVER = OVER
endmodule

module enable16 (
  input  ENA,
  input  [15:0] I,
  output [15:0] OUTP
);

  and and_1 (OUTP[0], I[0], ENA);
  and and_2 (OUTP[1], I[1], ENA);
  and and_3 (OUTP[2], I[2], ENA);
  and and_4 (OUTP[3], I[3], ENA);
  and and_5 (OUTP[4], I[4], ENA);
  and and_6 (OUTP[5], I[5], ENA);
  and and_7 (OUTP[6], I[6], ENA);
  and and_8 (OUTP[7], I[7], ENA);
  and and_9 (OUTP[8], I[8], ENA);
  and and_10 (OUTP[9], I[9], ENA);
  and and_11 (OUTP[10], I[10], ENA);
  and and_12 (OUTP[11], I[11], ENA);
  and and_13 (OUTP[12], I[12], ENA);
  and and_14 (OUTP[13], I[13], ENA);
  and and_15 (OUTP[14], I[14], ENA);
  and and_16 (OUTP[15], I[15], ENA);
endmodule

module enable1 (
  input  ENA,
  input  I,
  output OUTP
);

  and and_1 (OUTP, I, ENA);
endmodule

module addsub16 (
  input  [15:0] A,
  input  [15:0] B,
  input  CIN,
  input  SUB,
  output [15:0] OUTP,
  output COUT,
  output OVER
);

  wire A15N, ADD, add16_1_cout, and_1_out, and_2_out, B15, B15N, enable1_1_outp, enable1_2_outp,
       enable1_3_outp, enable1_4_outp, not_3_out, not_4_out, or_2_out, OUTP15N;
  wire [14:0] B_t;
  wire [15:0] enable16_1_outp, enable16_2_outp, not_2_out;

  not not_1 (ADD, SUB);
  assign not_2_out = ~B;  // NOT_Gate not_2, 16 bits wide
  not not_3 (not_3_out, CIN);
  enable16 enable16_1 (.ENA(ADD), .I(B), .OUTP(enable16_1_outp));
  enable16 enable16_2 (.ENA(SUB), .I(not_2_out), .OUTP(enable16_2_outp));
  enable1 enable1_1 (.I(CIN), .ENA(ADD), .OUTP(enable1_1_outp));
  enable1 enable1_2 (.I(not_3_out), .ENA(SUB), .OUTP(enable1_2_outp));
  assign {B15, B_t} = enable16_1_outp | enable16_2_outp;  // OR_Gate or_1, 16 bits wide
  or or_2 (or_2_out, enable1_1_outp, enable1_2_outp);
  add16 add16_1 (.A(A), .CIN(or_2_out), .B({B15, B_t}), .OUTP(OUTP), .COUT(add16_1_cout));
  enable1 enable1_3 (.I(add16_1_cout), .ENA(ADD), .OUTP(enable1_3_outp));
  not not_4 (not_4_out, add16_1_cout);
  enable1 enable1_4 (.I(not_4_out), .ENA(SUB), .OUTP(enable1_4_outp));
  not not_5 (A15N, A[15]);
  not not_6 (B15N, B15);
  not not_7 (OUTP15N, OUTP[15]);
  or or_3 (COUT, enable1_3_outp, enable1_4_outp);
  and and_1 (and_1_out, A[15], B15, OUTP15N);
  and and_2 (and_2_out, A15N, B15N, OUTP[15]);
  or or_4 (OVER, and_1_out, and_2_out);

  // Other names for the same wires on the sheet: B_t[15] = B15
endmodule
